# Fritzing sketch louis PCB (saved by Fritzing 0.9.4)
circuit board: 4.7501cm x 5.87cm
breadboards: 2

parts:
  MOTOR_Driver = L293D [package=THT]
  button = Round Pushbutton
  Crystal = Crystal [frequency="16 Mhz" package=THT]
  OUPUT = Header 6 [package=molex-1x6_lock]
  ATMEGA328 = atmega328 [package=dip]
  INPUT = Header 6 [package=molex-1x6_lock]
  C5 = Capacitor [package=cap-pth-small2]
  C6 = Capacitor [package=cap-pth-small2]
  Servo_Socket = RJ11 Jack [package=rj11-6]

nets:
  N1: MOTOR_Driver.Enable_1, ATMEGA328.D6_(PWM)
  N2: MOTOR_Driver.In_1, ATMEGA328.D4
  N3: MOTOR_Driver.Out_1_(_Controlled_by_Enable_1_), Servo_Socket.4
  N4: MOTOR_Driver.0V, button.leg1, OUPUT.2, ATMEGA328.GND, INPUT.2, C5.2, C6.2, Servo_Socket.5
  N5: MOTOR_Driver.Out_2_(_Controlled_by_Enable_1_), Servo_Socket.3
  N6: MOTOR_Driver.In_2, ATMEGA328.D7
  N7: MOTOR_Driver.+Vmotor, OUPUT.1, INPUT.1
  N8: MOTOR_Driver.+V, OUPUT.3, ATMEGA328.VCC, ATMEGA328.AVCC, ATMEGA328.AREF, INPUT.3, Servo_Socket.2
  N9: button.leg0, ATMEGA328.D5_(PWM)
  N10: Crystal.pin_0, ATMEGA328.XLAT1, C5.1
  N11: Crystal.pin_1, ATMEGA328.XLAT2, C6.1
  N12: OUPUT.4, ATMEGA328.D9_(PWM)
  N13: OUPUT.5, ATMEGA328.D8
  N14: ATMEGA328.D0_(RX), INPUT.5
  N15: ATMEGA328.D1_(TX), INPUT.4
  N16: ATMEGA328.D2, Servo_Socket.6
  N17: ATMEGA328.D3_(PWM), Servo_Socket.1
