# Fritzing sketch louis PCB version 1 (saved by Fritzing 0.9.4)
circuit board: 7.06774cm x 5.86387cm
breadboards: 2

parts:
  C5 = Capacitor [package=cap-pth-small2]
  C6 = Capacitor [package=cap-pth-small2]
  MOTOR_Driver = L293D [package=THT]
  Crystal = Crystal [frequency="16 Mhz" package=SMD]
  OUPUT = Header 6 [package=molex-1x6_lock]
  INPUT = Header 6 [part_number=test package=molex-1x6-ra]
  RJ11 = RJ11 Jack [package=rj11-6]
  ATMEGA328 = atmega328 [package=dip]
  Button = Pushbutton [package="[THT]"]

nets:
  N1: C5.1, Crystal.pin_0, ATMEGA328.XLAT1
  N2: C5.2, C6.2, MOTOR_Driver.0V, OUPUT.2, INPUT.2, RJ11.5, ATMEGA328.GND, ATMEGA328.D5_(PWM), Button.Pin_1, Button.Pin_2
  N3: C6.1, Crystal.pin_1, ATMEGA328.XLAT2
  N4: MOTOR_Driver.Enable_1, ATMEGA328.D6_(PWM)
  N5: MOTOR_Driver.In_1, RJ11.1, ATMEGA328.D3_(PWM), ATMEGA328.D4
  N6: MOTOR_Driver.Out_1_(_Controlled_by_Enable_1_), RJ11.4
  N7: MOTOR_Driver.Out_2_(_Controlled_by_Enable_1_), RJ11.3
  N8: MOTOR_Driver.In_2, ATMEGA328.D7
  N9: MOTOR_Driver.+Vmotor, OUPUT.1, INPUT.1
  N10: MOTOR_Driver.+V, OUPUT.3, INPUT.3, RJ11.2, ATMEGA328.VCC, ATMEGA328.AVCC, ATMEGA328.AREF
  N11: OUPUT.4, ATMEGA328.D9_(PWM)
  N12: OUPUT.5, ATMEGA328.D8
  N13: INPUT.4, ATMEGA328.D0_(RX)
  N14: INPUT.5, ATMEGA328.D1_(TX)
  N15: RJ11.6, ATMEGA328.D2

notes:
  ThreeDots, louis
